# Fritzing sketch Schema (saved by Fritzing 0.9.3b)
breadboards: 1

parts:
  Composant1 = Arduino Uno (Rev3)
  R1 = Rotary Potentiometer (Small) [maximum_resistance=100kΩ package=THT]
  J1 = Basic Servo

nets:
  N1: Composant1.A0, R1.wiper
  N2: Composant1.D3_PWM, J1.pulse
  N3: Composant1.5V, R1.leg1
  GND: Composant1.GND, R1.leg2, J1.gnd
