# Fritzing sketch Schema1 (saved by Fritzing 0.9.3b)
breadboards: 1

parts:
  Composant1 = Arduino Uno (Rev3)
  R1 = Rotary Potentiometer (Small) [maximum_resistance=100kΩ package=THT]
  J1 = Basic Servo
  hc-sr1 = hc-sr04

nets:
  N1: Composant1.A0, R1.wiper
  N2: Composant1.D11_PWM/MOSI, hc-sr1.Echo
  N3: Composant1.D2, hc-sr1.Trig
  N4: Composant1.D3_PWM, J1.pulse
  5V: Composant1.5V, R1.leg1, hc-sr1.VCC
  GND: Composant1.GND, R1.leg2, J1.gnd, hc-sr1.GND
